# Fritzing sketch 配線図 (saved by Fritzing 0.9.9b)
breadboards: 1

parts:
  R1 = Resistor [tolerance=±5% power=0.25 resistance=220 package=THT]
  LED1 = LED - 5mm [color="Red (633nm)" current=0.030 package="5 mm [THT]"]
  VCC1 = Battery
  IC1 = PICAXE-18X [package=THT]

nets:
  N1: R1.Pin_0, IC1.Serial_Out
  N2: R1.Pin_1, LED1.anode
  N3: LED1.cathode, VCC1.-, IC1.0V
  N4: VCC1.+, IC1.+V
